// Digital circuit lab2_part1.dig as structural Verilog
module lab2_part1 (
  input  inA_0,
  input  inA_1,
  input  inA_2,
  input  inA_3,
  input  inB_0,
  input  inB_1,
  input  inB_2,
  input  inB_3,
  output out0,
  output out1,
  output out2,
  output out3
);

  Multiplexer #(.Selector_Bits(2)) multiplexer_1 (
    .sel({inB_1, inB_0}), .in_0(inA_3), .in_1(inA_2), .in_2(inA_1), .in_3(inA_0), .out(out3));
  Multiplexer #(.Selector_Bits(2)) multiplexer_2 (
    .sel({inB_1, inB_0}), .in_0(inA_2), .in_1(inA_1), .in_2(inA_0), .in_3(inA_3), .out(out2));
  Multiplexer #(.Selector_Bits(2)) multiplexer_3 (
    .sel({inB_1, inB_0}), .in_0(inA_1), .in_1(inA_0), .in_2(inA_3), .in_3(inA_2), .out(out1));
  Multiplexer #(.Selector_Bits(2)) multiplexer_4 (
    .sel({inB_1, inB_0}), .in_0(inA_0), .in_1(inA_3), .in_2(inA_2), .in_3(inA_1), .out(out0));

  // Notes on the sheet:
  //   Interface (do not edit the content inside this box)
  //   Inputs
  //   Outputs
  //   Rotatee:
  //   Rotation amount:
  //   Result of Rotating  input A by the amount given by input B:
endmodule

/* Test case:
inA_3 inA_2 inA_1 inA_0 inB_3 inB_2 inB_1 inB_0  out3 out2 out1 out0
 0     1     0     0     1     1     0     0      0    1    0    0
 0     0     1     1     1     1     0     0      0    0    1    1  
 1     1     0     1     1     1     0     1      1    0    1    1  
 0     0     0     1     1     1     1     0      0    1    0    0   
 0     1     1     1     1     1     1     1      1    0    1    1   
 0     1     0     1     1     1     0     0      0    1    0    1 
 0     1     1     0     1     1     0     1      1    1    0    0 
 1     0     0     1     1     1     1     0      0    1    1    0 
 1     1     1     1     1     1     1     1      1    1    1    1 
*/

/* Test case:
inA_3 inA_2 inA_1 inA_0 inB_1 inB_0  out3 out2 out1 out0
 0     0     0     0     0     0      0    0    0    0  
 0     0     0     1     0     0      0    0    0    1  
 0     0     0     1     0     1      0    0    1    0  
 0     0     0     1     1     0      0    1    0    0  
 0     0     0     1     1     1      1    0    0    0   
 0     1     0     1     0     0      0    1    0    1  
 0     1     0     1     0     1      1    0    1    0  
 0     1     0     1     1     0      0    1    0    1  
 0     1     0     1     1     1      1    0    1    0   
*/
