// Digital circuit lab2_part2.dig as structural Verilog
module lab2_part2 (
  input  in0,
  input  in1,
  input  in2,
  input  in3,
  output seg_a,
  output seg_f,
  output seg_b,
  output seg_g,
  output seg_e,
  output seg_c,
  output seg_d,
  output seg_dp,
  output sign_a,
  output sign_f,
  output sign_b,
  output sign_g,
  output sign_e,
  output sign_c,
  output sign_d,
  output sign_dp
);

  wire and_1_out, and_3_out, and_4_out, and_5_out, and_6_out, and_7_out, and_8_out, and_9_out, and_10_out,
       and_11_out, and_12_out, and_13_out, multiplexer_1_out, multiplexer_2_out, multiplexer_3_out,
       multiplexer_4_out, not_1_out, not_2_out, not_3_out, not_4_out, not_5_out, not_6_out, not_7_out,
       not_8_out, xor_1_out, xor_2_out, xor_3_out, xor_4_out;

  Seven_Seg seven_seg_1 (.a(1'b0), .b(1'b0), .c(1'b0), .d(1'b0), .e(1'b0), .f(1'b0), .g(sign_g), .dp(1'b0));
  Seven_Seg seven_seg_2 (.a(seg_a), .b(seg_b), .c(seg_c), .d(seg_d), .e(seg_e), .f(seg_f), .g(seg_g), .dp(1'b0));
  not not_1 (not_1_out, in3);
  xor xor_1 (xor_1_out, and_1_out, not_1_out);
  not not_2 (not_2_out, in2);
  and and_1 (and_1_out, and_3_out, not_2_out);
  xor xor_2 (xor_2_out, and_3_out, not_2_out);
  and and_2 (sign_g, 1'b1, in3);
  Multiplexer multiplexer_1 (.sel(in3), .in_0(in3), .in_1(xor_1_out), .out(multiplexer_1_out));
  not not_3 (not_3_out, in1);
  and and_3 (and_3_out, and_4_out, not_3_out);
  not not_4 (not_4_out, multiplexer_1_out);
  xor xor_3 (xor_3_out, and_4_out, not_3_out);
  Multiplexer multiplexer_2 (.sel(in3), .in_0(in2), .in_1(xor_2_out), .out(multiplexer_2_out));
  not not_5 (not_5_out, multiplexer_2_out);
  Multiplexer multiplexer_3 (.sel(in3), .in_0(in1), .in_1(xor_3_out), .out(multiplexer_3_out));
  not not_6 (not_6_out, multiplexer_3_out);
  not not_7 (not_7_out, in0);
  and and_4 (and_4_out, 1'b1, not_7_out);
  Multiplexer multiplexer_4 (.sel(in3), .in_0(in0), .in_1(xor_4_out), .out(multiplexer_4_out));
  not not_8 (not_8_out, multiplexer_4_out);
  xor xor_4 (xor_4_out, 1'b1, not_7_out);
  and and_5 (and_5_out, multiplexer_2_out, not_6_out);
  and and_6 (and_6_out, multiplexer_2_out, not_8_out);
  and and_7 (and_7_out, multiplexer_2_out, multiplexer_4_out);
  and and_8 (and_8_out, not_5_out, not_8_out);
  and and_9 (and_9_out, multiplexer_3_out, multiplexer_4_out);
  and and_10 (and_10_out, not_6_out, not_8_out);
  and and_11 (and_11_out, multiplexer_3_out, not_8_out);
  and and_12 (and_12_out, not_5_out, multiplexer_3_out);
  and and_13 (and_13_out, multiplexer_4_out, and_5_out);
  or or_1 (seg_a, and_7_out, and_8_out, multiplexer_1_out, multiplexer_3_out);
  or or_2 (seg_b, and_9_out, not_5_out, and_10_out);
  or or_3 (seg_c, multiplexer_2_out, not_6_out, multiplexer_4_out);
  or or_4 (seg_d, multiplexer_1_out, and_8_out, and_11_out, and_12_out, and_13_out);
  or or_5 (seg_f, and_10_out, and_6_out, and_5_out, multiplexer_1_out);
  or or_6 (seg_g, and_11_out, and_5_out, multiplexer_1_out, and_12_out);
  or or_7 (seg_e, and_11_out, and_8_out);

  assign seg_dp = 1'b0;
  assign sign_a = 1'b0;
  assign sign_b = 1'b0;
  assign sign_c = 1'b0;
  assign sign_d = 1'b0;
  assign sign_dp = 1'b0;
  assign sign_e = 1'b0;
  assign sign_f = 1'b0;

  // Notes on the sheet:
  //   Interface (do not edit the content inside this box)
  //   Outputs:
  //   Inputs
  //   Sign
  //   Decimal Number
endmodule

/* Test case:
in3 in2 in1 in0  sign_a sign_b sign_c sign_d sign_e sign_f sign_g  seg_a seg_b seg_c seg_d seg_e seg_f seg_g
 1   1  0   1     0      0      0      0      0      0      1       1     1     1     1     1     1     1
*/
